// Logisim project FA.circ as structural Verilog
module HA (
  input  A,
  input  B,
  output SUM,
  output CARRY
);

  xor xor_1 (SUM, A, B);
  and and_1 (CARRY, A, B);
endmodule

module FA (
  input  CI,
  input  X,
  input  Y,
  output SUM,
  output CO
);

  wire ha_1_carry, ha_1_sum, ha_2_carry;

  HA ha_1 (.A(X), .B(Y), .SUM(ha_1_sum), .CARRY(ha_1_carry));
  HA ha_2 (.A(CI), .B(ha_1_sum), .SUM(SUM), .CARRY(ha_2_carry));
  or or_1 (CO, ha_2_carry, ha_1_carry);
endmodule
