// Logisim project AIMLS.circ as structural Verilog: 1 circuit, main circuit main
module main (
  input  A,
  input  B,
  input  C,
  input  D,
  output Z
);

  wire and_1_out, not_1_out, not_2_out, or_1_out;

  not not_1 (not_1_out, C);
  not not_2 (not_2_out, D);
  or or_1 (or_1_out, A, B);
  and and_1 (and_1_out, not_1_out, not_2_out);
  and and_2 (Z, or_1_out, and_1_out);

  // Notes on the sheet:
  //   Aaron Mahoney
  //   G
  //   E
  //   F
  //   H
endmodule
