// Logisim project Encoder.circ as structural Verilog: 1 circuit, main circuit main
module main (
  input  D3,
  input  D2,
  input  D1,
  input  D0,
  output A0,
  output A1,
  output VALID
);

  wire and_1_out, not_1_out;

  not not_1 (not_1_out, D2);
  Priority_Encoder #(.select(2)) priority_encoder_1 ();  // open: in0, in1, in2, in3, out, gs, en_out, en_in
  and and_1 (and_1_out, not_1_out, D1);
  or or_1 (A0, D3, and_1_out);
  or or_2 (A1, D3, D2);
  or or_3 (VALID, D3, D2, D1, D0);
endmodule
